# Fritzing sketch fritzing-sketch (saved by Fritzing 0.9.3b)
breadboards: 1

parts:
  LED1 = smd LED [color="Red (633nm)" package="0603 [SMD]"]
  LCD1 = LCD screen
  Part2 = Soil Moisture Sensor
  DHT11 = DHT11 Humitidy and Temperature Sensor
  Raspberry_Pi_1 = Raspberry Pi 3 [part_number=RPI-3-V1.2]  # not connected
  Part1 = Arduino Uno (Rev3)
  R1 = Resistor [tolerance=±5% resistance=10k package="0603 [SMD]"]
  LCM1602_IIC1 = LCM1602 IIC [part_number="LCM1602 IIC" chip_label="LCM1602 IIC" package="DIP (Dual Inline) [THT]"]
  R2 = Resistor [tolerance=±5% resistance=220 package="0402 [SMD]"]
  D1 = Diode [package=diode-1n4001]
  Q1 = NPN-Transistor [package="TO92 [THT]"]
  M1 = DC Motor
  R3 = Resistor [tolerance=±5% resistance=220 package="1206 [SMD]"]
  LED2 = smd LED [color="Orange (620nm)" package="0603 [SMD]"]
  R4 = Resistor [tolerance=±5% resistance=220 package="1206 [SMD]"]
  Part3 = Adafruit Pi T-Cobbler [part_number="Adafruit #1754 and #1105"]

nets:
  N1: LED1.cathode, R3.Pin_1
  N2: LED1.anode, Part1.D13/SCK
  VSS: LCD1.VSS, LCM1602_IIC1.VSS
  VDD: LCD1.VDD, LCM1602_IIC1.VDD
  N3: LCD1.V0, LCM1602_IIC1.V0
  N4: LCD1.RS, LCM1602_IIC1.RS
  N5: LCD1.R/W, LCM1602_IIC1.RW
  N6: LCD1.E, LCM1602_IIC1.E
  N7: LCD1.DB0, LCM1602_IIC1.D0
  N8: LCD1.DB1, LCM1602_IIC1.D1
  N9: LCD1.DB2, LCM1602_IIC1.D2
  N10: LCD1.DB3, LCM1602_IIC1.D3
  N11: LCD1.DB4, LCM1602_IIC1.D4
  N12: LCD1.DB5, LCM1602_IIC1.D5
  N13: LCD1.DB6, LCM1602_IIC1.D6
  N14: LCD1.DB7, LCM1602_IIC1.D7
  N15: LCD1.LED+, LCM1602_IIC1.A
  N16: LCD1.LED-, LCM1602_IIC1.K
  GND: Part2.GND, DHT11.GND, Part1.GND, Q1.E, R3.Pin_0, R4.Pin_0
  N17: Part2.SIG, Part1.A0
  VCC: Part2.VCC, DHT11.VDD, Part1.5V, R1.Pin_0, D1.C, M1.pin_1
  N18: DHT11.DATA, Part1.D7, R1.Pin_1
  N19: Part1.D12/MISO, LED2.anode
  N20: Part1.D3_PWM, R2.Pin_0
  GND_2: LCM1602_IIC1.GND, Part3.GND
  N21: LCM1602_IIC1.VCC, Part3.5.0V
  N22: LCM1602_IIC1.SDA, Part3.SDA
  N23: LCM1602_IIC1.SCL, Part3.SCL
  N24: LCM1602_IIC1.LED_A, LCM1602_IIC1.LED_B
  N25: R2.Pin_1, Q1.C
  N26: Q1.B, M1.pin_2
  N27: LED2.cathode, R4.Pin_1

custom parts:
  DHT11 Humitidy and Temperature Sensor: DHT11 Humidity and Temperature Sensor
  LCM1602 IIC: I2C-Module to use a 1602 or 2004 LCD on with the wire.h libory Serial LCD Modul
  Adafruit Pi T-Cobbler: Now that you've finally got your hands on a Raspberry Pi® , you're probably itching to make some fun embedded computer projects with it. What you need is an assembled add on prototyping Pi T-Cobbler from Adafruit, which can break out all those tasty power, GPIO, I2C and SPI pins from the 26 pin header onto a solderless breadboard. This mini kit will make "cobbling together" prototypes with the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
